# Fritzing sketch SHMI_ROBOT (saved by Fritzing 0.9.3b)
breadboards: 1

parts:
  S1 = H-Bridge with L298N
  Part1 = Arduino Uno (Rev3)
  LED1 = LED - 5mm [color="Infrared (850nm)" package="5 mm [THT]"]
  Part2 = Bluetooth HC-05 Macho
  M1 = DC Motor
  M2 = DC Motor

nets:
  12V: S1.12V, Part1.VIN
  GND: S1.GND, Part1.GND, LED1.cathode, Part2.GND
  N1: S1.ENA, S1.ENA-5V
  N2: S1.IN1, Part1.D7
  N3: S1.IN2, Part1.D6_PWM
  N4: S1.IN3, Part1.D5_PWM
  N5: S1.IN4, Part1.D4
  N6: S1.ENB, S1.ENB-5V
  N7: S1.M1-01, M2.pin_2
  N8: S1.M1-02, M2.pin_1
  N9: S1.M2-01, M1.pin_2
  N10: S1.M2-02, M1.pin_1
  N11: Part1.D13/SCK, LED1.anode
  N12: Part1.D0/RX, Part2.TXD
  N13: Part1.D1/TX, Part2.RXD
  5V: Part1.5V, Part2.VCC

notes:
  In1
  In2
  In3
  In4
  +
  OUT1
  OUT2
  OUT3
  OUT4
  Мотор
  Светодиод
  Драйвер
  моторов
  Контроллер
  Bluetooth

custom parts:
  H-Bridge with L298N: h-bridge
