# Fritzing sketch SHMI_ROBOT_SERVO (saved by Fritzing 0.9.3b)
breadboards: 1

parts:
  J1 = Basic Servo
  J2 = Basic Servo
  J3 = Basic Servo
  J4 = Basic Servo
  Part1 = Arduino Uno (Rev3)
  S1 = H-Bridge with L298N
  HEF3 = HEF4094 [package="DIP16 [THT]"]
  K2 = Relay [part_number=FRS1B-S package=THT]
  Part2 = Bluetooth HC-05 Macho
  M1 = DC Motor
  M2 = DC Motor

nets:
  GND: J1.gnd, J2.gnd, J3.gnd, J4.gnd, HEF3.OUT-
  VCC: J1.vcc, J2.vcc, J3.vcc, J4.vcc, HEF3.OUT+
  N1: J1.pulse, Part1.D9_PWM
  N2: J2.pulse, Part1.D8
  N3: J3.pulse, Part1.D7
  N4: J4.pulse, Part1.D6_PWM
  N5: Part1.D13/SCK, K2.COIL1
  N6: Part1.D0/RX, Part2.TXD
  N7: Part1.D1/TX, Part2.RXD
  N8: Part1.D2, S1.IN4
  N9: Part1.D3_PWM, S1.IN3
  N10: Part1.D4, S1.IN2
  N11: Part1.D5_PWM, S1.IN1
  5V: Part1.5V, Part2.VCC
  GND_2: Part1.GND, S1.GND, HEF3.IN-, K2.COIL2, Part2.GND
  N12: Part1.VIN, K2.C1
  N13: S1.12V, K2.B
  N14: S1.ENA, S1.ENA-5V
  N15: S1.ENB, S1.ENB-5V
  N16: S1.M1-01, M1.pin_2
  N17: S1.M1-02, M1.pin_1
  N18: S1.M2-01, M2.pin_2
  N19: S1.M2-02, M2.pin_1
  N20: HEF3.IN+, K2.A

notes:
  In1
  In2
  In3
  In4
  OUT4
  OUT3
  OUT2
  OUT1
  Драйвер
  моторов
  IN+
  IN-
  OUT+
  OUT-
  5V
  5.3V
  +12V
  Контроллер
  Мотор
  Реле
  Bluetooth
  Сервопривод
  Преобразователь тока
  +
  S1
  S2
  S3
  S4

custom parts:
  H-Bridge with L298N: h-bridge
  HEF4094: (Identical part HCF4094) The HEF4094 is an 8-stage serial shift register. It has a storage latch associated with each stage for strobing data from the serial input to parallel buffered 3-state outputs. The parallel outputs may be connected directly to common bus lines. Data is shifted on positive-going clock transitions. The data in each shift register stage is transferred to the storage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
  Relay: An SPDT relay.
